# Fritzing sketch placa drivers (saved by Fritzing 0.9.2b)
perfboards: 2

parts:
  MD09B1 = A4988 Stepper Motor Driver Carrier  # not connected
  C1 = Electrolytic Capacitor [capacitance=100µF voltage=16V package="100 mil [THT, electrolytic]"]  # not connected
  12V = Power plug  # not connected
  MD09B3 = A4988 Stepper Motor Driver Carrier  # not connected
  MD09B4 = A4988 Stepper Motor Driver Carrier
  MD09B6 = A4988 Stepper Motor Driver Carrier
  MD09B7 = A4988 Stepper Motor Driver Carrier
  MD09B9 = A4988 Stepper Motor Driver Carrier
  MD09B10 = A4988 Stepper Motor Driver Carrier
  MD09B11 = A4988 Stepper Motor Driver Carrier
  J38 = female pin header, 1 pin [form="♀ (female)"]  # not connected
  J36 = male pin header, 4 pins [form="♂ (male)"]  # not connected
  J32 = male pin header, 4 pins [form="♂ (male)"]  # not connected
  J34 = male pin header, 4 pins [form="♂ (male)"]  # not connected
  J33 = male pin header, 4 pins [form="♂ (male)"]  # not connected
  J58 = male pin header, 1 pin [form="♂ (male)"]  # not connected
  J43 = male pin header, 2 pins [form="♂ (male)"]  # not connected
  J40 = male pin header, 1 pin [form="♂ (male)"]  # not connected
  J42 = male pin header, 2 pins [form="♂ (male)"]  # not connected
  J37 = male pin header, 1 pin [form="♂ (male)"]  # not connected
  J46 = male pin header, 2 pins [form="♂ (male)"]  # not connected
  J41 = male pin header, 1 pin [form="♂ (male)"]  # not connected
  J44 = male pin header, 2 pins [form="♂ (male)"]  # not connected
  J3 = male pin header, 1 pin [form="♂ (male)"]  # not connected
  J4 = male pin header, 2 pins [form="♂ (male)"]  # not connected
  J13 = male pin header, 1 pin [form="♂ (male)"]  # not connected
  J14 = male pin header, 2 pins [form="♂ (male)"]  # not connected
  J18 = male pin header, 1 pin [form="♂ (male)"]  # not connected
  J19 = male pin header, 2 pins [form="♂ (male)"]  # not connected
  J23 = male pin header, 1 pin [form="♂ (male)"]  # not connected
  J24 = male pin header, 2 pins [form="♂ (male)"]  # not connected
  J28 = male pin header, 1 pin [form="♂ (male)"]  # not connected
  J29 = male pin header, 2 pins [form="♂ (male)"]  # not connected
  J1 = male pin header, 4 pins [form="♂ (male)"]  # not connected
  J12 = male pin header, 4 pins [form="♂ (male)"]  # not connected
  J17 = male pin header, 4 pins [form="♂ (male)"]  # not connected
  J22 = male pin header, 4 pins [form="♂ (male)"]  # not connected
  J27 = male pin header, 4 pins [form="♂ (male)"]  # not connected
  J5 = male pin header, 1 pin [form="♂ (male)"]  # not connected
  J57 = male pin header, 1 pin [form="♂ (male)"]  # not connected
  MD09B5 = A4988 Stepper Motor Driver Carrier
  J59 = male pin header, 1 pin [form="♂ (male)"]  # not connected

nets:
  N1: MD09B4.RESET, MD09B4.SLEEP
  N2: MD09B6.RESET, MD09B6.SLEEP
  N3: MD09B7.RESET, MD09B7.SLEEP
  N4: MD09B9.RESET, MD09B9.SLEEP
  N5: MD09B10.RESET, MD09B10.SLEEP
  N6: MD09B11.RESET, MD09B11.SLEEP
  N7: MD09B5.RESET, MD09B5.SLEEP
